# Fritzing sketch prototype (saved by Fritzing 0.9.5d)
breadboards: 1

parts:
  Componente1 = Arduino Uno (Rev3) - ICSP
  Grove1 = Grove OLED 128x96
  ZS-042_RTC1 = ZS-042 RTC Module

nets:
  N1: Componente1.A4/SDA, Grove1.SDA, ZS-042_RTC1.SDA
  N2: Componente1.A5/SCL, Grove1.SCL, ZS-042_RTC1.SCL
  GND: Componente1.GND, Grove1.GND, ZS-042_RTC1.GND
  VCC: Componente1.5V, Grove1.VCC, ZS-042_RTC1.VCC

notes:
  Tiny RTC
  Display Oled 0.96 I2c Ssd1306
